# Fritzing sketch circuit (saved by Fritzing 0.9.10b)

parts:
  Part1 = Arduino Uno (Rev3)
  Part2 = Black Joystick KY-023
  OLED1 = OLED 128x64 I2C Monochrome Display GND-VDD
  J1 = Piezo Speaker

nets:
  N1: Part1.A1, Part2.VRx
  N2: Part1.A4/SDA, OLED1.SDA
  N3: Part1.A5/SCL, OLED1.SCK
  N4: Part1.D11_PWM/MOSI, J1.pin2
  N5: Part1.D4, Part2.SW
  5V: Part1.5V, OLED1.VDD
  GND: Part1.GND, Part2.GND, OLED1.GND

custom parts:
  Black Joystick KY-023: Description: The joystick is a combination of 2 analoog potentiometer and a digital switch. Arduino GND --> Module pin - Arduino +5V --> Module pin +5V Arduino Analoog 0 --> Module VRx Arduino Analoog 1 --> Module VRy Arduino Digital --> Module SW Dimensions: 1" x 1.25"
  OLED 128x64 I2C Monochrome Display GND-VDD: OLED 128x64 I2C Monochrome Display. Note: there are two variants of this part, this one is the GND VDD SCK SDA variant. The other is VDD GND SCK SDA. Make sure you select the part that matches your module as using the incorrect part will probably destroy your module! In addition the mounting holes are marked on silkscreen but not by default drilled. If you want drilled mounting holes, copy a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
